# Fritzing sketch Schema (saved by Fritzing 0.9.3b)
breadboards: 1

parts:
  R1 = Resistor [tolerance=±5% resistance=1k package=THT]
  R2 = Resistor [tolerance=±5% resistance=1k package=THT]
  U1 = ESP8266 NodeMCU LoLin module
  5v_Regulator = 4 x AAA Battery Mount
  Reset_Button = Round Pushbutton
  Lower_Floating = Round Pushbutton
  Higher_Floating1 = Round Pushbutton
  Componente1 = Passive Buzzer
  Mod1 = KY-016 RGB Full Color LED Module [package="Breakout board"]

nets:
  N1: R1.Pin_0, U1.D6, Lower_Floating.leg1
  N2: R1.Pin_1, R2.Pin_1, U1.3V3, Componente1.NC
  N3: R2.Pin_0, U1.D7, Higher_Floating1.leg1
  N4: U1.D0, Mod1.G
  N5: U1.D2, Mod1.B
  GND: U1.GND, 5v_Regulator.-, Reset_Button.leg1, Lower_Floating.leg0, Higher_Floating1.leg0, Componente1.GND, Mod1.-
  N6: U1.D5, Componente1.S
  N7: U1.RST, Reset_Button.leg0

custom parts:
  ESP8266 NodeMCU LoLin module: ESP8266 based NodeMCU
  KY-016 RGB Full Color LED Module: KY-016 Arduino full color 5mm RGB LED, different colors can be obtained by mixing the three primary colors.
